# Fritzing sketch fkaudio (saved by Fritzing 0.9.3b)
circuit board: 3.2cm x 4.4cm
breadboards: 1

parts:
  DA15F = DB15 Connector [package=db15]
  WRITE = Audio Jack (TRS) 3.5mm [package="4Ucon 08780 [THT]"]
  READ = Audio Jack (TRS) 3.5mm [package="4Ucon 08780 [THT]"]
  4069 = IC, DIP package, 14 pins [chip_label=IC]
  103 = Ceramic Capacitor [capacitance=100nF package="100 mil [THT, multilayer]"]
  1M = Resistor [tolerance=±5% resistance=220 package=THT]
  1K = Resistor [tolerance=±5% resistance=220 package=THT]
  D1 = Rectifier Diode [part_number=1N4001 package="300 mil [THT]"]
  103_2 = Ceramic Capacitor [capacitance=100nF package="100 mil [THT, multilayer]"]
  20K = Resistor [tolerance=±5% resistance=220 package=THT]
  100K = Resistor [tolerance=±5% resistance=220 package=THT]
  103_3 = Ceramic Capacitor [capacitance=100nF package="100 mil [THT, multilayer]"]

nets:
  N1: DA15F.1, WRITE.Sleeve, READ.Sleeve, 4069.pin7, 1K.Pin_0, 103_3.0
  N2: DA15F.10, 4069.pin1
  N3: DA15F.12, 103.0
  N4: DA15F.13, 4069.pin6
  N5: DA15F.15, 4069.pin9, 4069.pin11, 4069.pin13, 4069.pin14
  N6: WRITE.Tip, 1M.Pin_1, 1K.Pin_1
  N7: READ.Tip, 103_2.1
  N8: 4069.pin2, D1.anode
  N9: 4069.pin3, 20K.Pin_1, 100K.Pin_1
  N10: 4069.pin4, 4069.pin5, 100K.Pin_0, 103_3.1
  N11: 103.1, 1M.Pin_0
  N12: D1.cathode, 103_2.0, 20K.Pin_0

notes:
  Famicom Keyboard Emulator
  Cassette Interface

custom parts:
  DB15 Connector: DB15 Connector Standard DB15 (D-Sub 15) pc midi or gameport connector. Can be used for old PC compatible joystic.
