# Fritzing sketch battery (saved by Fritzing 0.9.3b)
circuit board: 5cm x 2.8cm
breadboards: 1

parts:
  Pad1 = Pad [width=5 height=10 connect=center]
  Pad2 = Pad [width=5 height=10 connect=center]
  Pad3 = Pad [width=5 height=10 connect=center]
  Pad4 = Pad [width=5 height=10 connect=center]
  BAT1 = Battery Holders [package=battcom_20mm_pth]
  Pad6 = Pad [width=2 height=2 connect=center]
  Pad7 = Pad [width=2 height=2 connect=center]
  Pad10 = Pad [width=2 height=2 connect=center]
  Pad11 = Pad [width=2 height=2 connect=center]
  Pad12 = Pad [width=2 height=2 connect=center]
  Pad14 = Pad [width=2 height=2 connect=center]
  Pad15 = Pad [width=2 height=2 connect=center]
  Pad16 = Pad [width=2 height=2 connect=center]
  J1 = female pin header, 1 pin [form="♀ (female)"]
  J2 = female pin header, 1 pin [form="♀ (female)"]
  J3 = female pin header, 1 pin [form="♀ (female)"]
  J4 = female pin header, 1 pin [form="♀ (female)"]

nets:
  N1: Pad1.pad, Pad7.pad
  N2: Pad2.pad, Pad11.pad
  N3: Pad3.pad, Pad14.pad
  N4: Pad4.pad, Pad15.pad
  N5: BAT1.+, Pad6.pad, Pad12.pad, J1.pin1, J3.pin1
  N6: BAT1.-, Pad10.pad, Pad16.pad, J2.pin1, J4.pin1

notes:
  -
  +
