# Fritzing sketch fcextender (saved by Fritzing 0.9.3b)
circuit board: 7.86cm x 3.3cm
breadboards: 1

parts:
  J9 = single row smd female pin header, 15 pins [form="♀ (female)"]
  J10 = single row smd female pin header, 15 pins [form="♀ (female)"]
  J11 = single row smd female pin header, 15 pins [form="♀ (female)"]
  J12 = single row smd female pin header, 15 pins [form="♀ (female)"]
  J13 = single row smd female pin header, 15 pins [form="♀ (female)"]
  J14 = single row smd female pin header, 15 pins [form="♀ (female)"]
  J15 = single row smd female pin header, 15 pins [form="♀ (female)"]
  J16 = single row smd female pin header, 15 pins [form="♀ (female)"]
  J17 = single row smd female pin header, 15 pins [form="♀ (female)"]
  J18 = single row smd female pin header, 15 pins [form="♀ (female)"]
  J19 = single row smd female pin header, 15 pins [form="♀ (female)"]
  J20 = single row smd female pin header, 15 pins [form="♀ (female)"]
  J21 = single row smd female pin header, 15 pins [form="♀ (female)"]
  J22 = single row smd female pin header, 15 pins [form="♀ (female)"]
  J23 = single row smd female pin header, 15 pins [form="♀ (female)"]
  J24 = single row smd female pin header, 15 pins [form="♀ (female)"]

nets:
  N1: J9.pin1, J10.pin15, J17.pin1, J18.pin15
  N2: J9.pin2, J10.pin14, J17.pin2, J18.pin14
  N3: J9.pin3, J10.pin13, J17.pin3, J18.pin13
  N4: J9.pin4, J10.pin12, J17.pin4, J18.pin12
  N5: J9.pin5, J10.pin11, J17.pin5, J18.pin11
  N6: J9.pin6, J10.pin10, J17.pin6, J18.pin10
  N7: J9.pin7, J10.pin9, J17.pin7, J18.pin9
  N8: J9.pin8, J10.pin8, J17.pin8, J18.pin8
  N9: J9.pin9, J10.pin7, J17.pin9, J18.pin7
  N10: J9.pin10, J10.pin6, J17.pin10, J18.pin6
  N11: J9.pin11, J10.pin5, J17.pin11, J18.pin5
  N12: J9.pin12, J10.pin4, J17.pin12, J18.pin4
  N13: J9.pin13, J10.pin3, J17.pin13, J18.pin3
  N14: J9.pin14, J10.pin2, J17.pin14, J18.pin2
  N15: J9.pin15, J10.pin1, J17.pin15, J18.pin1
  N16: J11.pin1, J12.pin15, J19.pin1, J20.pin15
  N17: J11.pin2, J12.pin14, J19.pin2, J20.pin14
  N18: J11.pin3, J12.pin13, J19.pin3, J20.pin13
  N19: J11.pin4, J12.pin12, J19.pin4, J20.pin12
  N20: J11.pin5, J12.pin11, J19.pin5, J20.pin11
  N21: J11.pin6, J12.pin10, J19.pin6, J20.pin10
  N22: J11.pin7, J12.pin9, J19.pin7, J20.pin9
  N23: J11.pin8, J12.pin8, J19.pin8, J20.pin8
  N24: J11.pin9, J12.pin7, J19.pin9, J20.pin7
  N25: J11.pin10, J12.pin6, J19.pin10, J20.pin6
  N26: J11.pin11, J12.pin5, J19.pin11, J20.pin5
  N27: J11.pin12, J12.pin4, J19.pin12, J20.pin4
  N28: J11.pin13, J12.pin3, J19.pin13, J20.pin3
  N29: J11.pin14, J12.pin2, J19.pin14, J20.pin2
  N30: J11.pin15, J12.pin1, J19.pin15, J20.pin1
  N31: J13.pin1, J14.pin15, J21.pin1, J22.pin15
  N32: J13.pin2, J14.pin14, J21.pin2, J22.pin14
  N33: J13.pin3, J14.pin13, J21.pin3, J22.pin13
  N34: J13.pin4, J14.pin12, J21.pin4, J22.pin12
  N35: J13.pin5, J14.pin11, J21.pin5, J22.pin11
  N36: J13.pin6, J14.pin10, J21.pin6, J22.pin10
  N37: J13.pin7, J14.pin9, J21.pin7, J22.pin9
  N38: J13.pin8, J14.pin8, J21.pin8, J22.pin8
  N39: J13.pin9, J14.pin7, J21.pin9, J22.pin7
  N40: J13.pin10, J14.pin6, J21.pin10, J22.pin6
  N41: J13.pin11, J14.pin5, J21.pin11, J22.pin5
  N42: J13.pin12, J14.pin4, J21.pin12, J22.pin4
  N43: J13.pin13, J14.pin3, J21.pin13, J22.pin3
  N44: J13.pin14, J14.pin2, J21.pin14, J22.pin2
  N45: J13.pin15, J14.pin1, J21.pin15, J22.pin1
  N46: J15.pin1, J16.pin15, J23.pin1, J24.pin15
  N47: J15.pin2, J16.pin14, J23.pin2, J24.pin14
  N48: J15.pin3, J16.pin13, J23.pin3, J24.pin13
  N49: J15.pin4, J16.pin12, J23.pin4, J24.pin12
  N50: J15.pin5, J16.pin11, J23.pin5, J24.pin11
  N51: J15.pin6, J16.pin10, J23.pin6, J24.pin10
  N52: J15.pin7, J16.pin9, J23.pin7, J24.pin9
  N53: J15.pin8, J16.pin8, J23.pin8, J24.pin8
  N54: J15.pin9, J16.pin7, J23.pin9, J24.pin7
  N55: J15.pin10, J16.pin6, J23.pin10, J24.pin6
  N56: J15.pin11, J16.pin5, J23.pin11, J24.pin5
  N57: J15.pin12, J16.pin4, J23.pin12, J24.pin4
  N58: J15.pin13, J16.pin3, J23.pin13, J24.pin3
  N59: J15.pin14, J16.pin2, J23.pin14, J24.pin2
  N60: J15.pin15, J16.pin1, J23.pin15, J24.pin1

notes:
  FAMICOM EXTENDER
