# Fritzing sketch fambasic (saved by Fritzing 0.9.3b)
circuit board: 9.52cm x 9.02015cm
breadboards: 1

parts:
  J1 = single row smd female pin header, 15 pins [form="♀ (female)"]
  J2 = single row smd female pin header, 15 pins [form="♀ (female)"]
  J3 = single row smd female pin header, 15 pins [form="♀ (female)"]
  J4 = single row smd female pin header, 15 pins [form="♀ (female)"]
  J6 = single row smd female pin header, 15 pins [form="♀ (female)"]
  J7 = single row smd female pin header, 15 pins [form="♀ (female)"]
  J8 = single row smd female pin header, 15 pins [form="♀ (female)"]
  J5 = single row smd female pin header, 15 pins [form="♀ (female)"]
  C1 = Ceramic Capacitor [capacitance=100nF package="100 mil [THT, multilayer]"]
  C2 = Ceramic Capacitor [capacitance=100nF package="100 mil [THT, multilayer]"]
  C3 = Ceramic Capacitor [capacitance=100nF package="100 mil [THT, multilayer]"]
  C4 = Ceramic Capacitor [capacitance=100nF package="100 mil [THT, multilayer]"]
  C5 = Ceramic Capacitor [capacitance=100nF package="100 mil [THT, multilayer]"]
  C6 = Ceramic Capacitor [capacitance=100nF package="100 mil [THT, multilayer]"]
  D2 = Rectifier Diode [part_number=1N4001 package="300 mil [THT]"]
  D1 = Rectifier Diode [part_number=1N4001 package="300 mil [THT]"]
  R1 = Resistor [tolerance=±5% resistance=5.1k package=THT]
  BAT = Battery
  IC1 = IC, DIP package, 10 pins [chip_label=IC]
  R2 = Resistor [tolerance=±5% resistance=220 package=THT]
  R3 = Resistor [tolerance=±5% resistance=220 package=THT]
  R4 = Resistor [tolerance=±5% resistance=220 package=THT]
  R5 = Resistor [tolerance=±5% resistance=220 package=THT]
  Pad2 = Pad [width=2 height=2 connect=center]
  Pad3 = Pad [width=2 height=2 connect=center]
  Pad4 = Pad [width=2 height=2 connect=center]
  Pad5 = Pad [width=2 height=2 connect=center]
  Pad6 = Pad [width=2 height=2 connect=center]
  Pad7 = Pad [width=2 height=2 connect=center]
  Pad8 = Pad [width=2 height=2 connect=center]
  Pad9 = Pad [width=2 height=2 connect=center]
  Pad10 = Pad [width=2 height=2 connect=center]
  Pad11 = Pad [width=2 height=2 connect=center]
  Pad12 = Pad [width=2 height=2 connect=center]
  Pad13 = Pad [width=2 height=2 connect=center]
  Pad14 = Pad [width=2 height=2 connect=center]
  Pad15 = Pad [width=2 height=2 connect=center]
  Pad16 = Pad [width=2 height=2 connect=center]
  Pad17 = Pad [width=2 height=2 connect=center]
  Pad18 = Pad [width=2 height=2 connect=center]
  Pad19 = Pad [width=2 height=2 connect=center]
  Pad20 = Pad [width=2 height=2 connect=center]
  Pad21 = Pad [width=2 height=2 connect=center]
  Pad22 = Pad [width=2 height=2 connect=center]
  Pad23 = Pad [width=2 height=2 connect=center]
  Pad24 = Pad [width=2 height=2 connect=center]
  Pad25 = Pad [width=2 height=2 connect=center]
  Pad26 = Pad [width=2 height=2 connect=center]
  Pad27 = Pad [width=2 height=2 connect=center]
  Pad28 = Pad [width=2 height=2 connect=center]
  IC1_2 = IC, DIP package, 28 pins [chip_label=IC]
  IC2 = IC, DIP package, 32 pins [chip_label=IC]
  IC3 = IC, DIP package, 32 pins [chip_label=IC]
  IC4 = IC, DIP package, 14 pins [chip_label=IC]
  IC5 = IC, DIP package, 32 pins [chip_label=IC]

nets:
  N1: J1.pin1, J2.pin15, J3.pin15, J4.pin1, C1.0, C2.1, C3.0, C4.0, C5.0, C6.0, BAT.-, IC1.pin6, IC1.pin7, IC1.pin8, IC1.pin9, Pad7.pad, Pad11.pad, Pad14.pad, IC1_2.pin14, IC1_2.pin22, IC2.pin16, IC3.pin16, IC4.pin7, IC5.pin16
  N2: J1.pin2, J2.pin14, Pad8.pad, IC2.pin25, IC3.pin25
  N3: J1.pin3, J2.pin13, IC1_2.pin21, IC2.pin23, IC3.pin23
  N4: J1.pin4, J2.pin12, IC1_2.pin24, IC2.pin26, IC3.pin26
  N5: J1.pin5, J2.pin11, IC1_2.pin25, IC2.pin27, IC3.pin27
  N6: J1.pin6, J2.pin10, IC1_2.pin3, IC2.pin5, IC3.pin5
  N7: J1.pin7, J2.pin9, IC1_2.pin4, IC2.pin6, IC3.pin6
  N8: J1.pin8, J2.pin8, IC1_2.pin5, IC2.pin7, IC3.pin7
  N9: J1.pin9, J2.pin7, IC1_2.pin6, IC2.pin8, IC3.pin8
  N10: J1.pin10, J2.pin6, IC1_2.pin7, IC2.pin9, IC3.pin9
  N11: J1.pin11, J2.pin5, IC1_2.pin8, IC2.pin10, IC3.pin10
  N12: J1.pin12, J2.pin4, IC1_2.pin9, IC2.pin11, IC3.pin11
  N13: J1.pin13, J2.pin3, IC1_2.pin10, IC2.pin12, IC3.pin12
  N14: J1.pin14, J2.pin2, Pad10.pad, IC1_2.pin27
  N15: J1.pin15, J2.pin1
  N16: J3.pin1, J4.pin15, J6.pin15, J7.pin1, C2.0, C3.1, C4.1, C6.1, D2.anode, R2.Pin_0, R3.Pin_0, R4.Pin_0, R5.Pin_0, Pad2.pad, Pad26.pad, Pad27.pad, Pad28.pad, IC2.pin1, IC2.pin30, IC2.pin31, IC2.pin32, IC3.pin1, IC3.pin30, IC3.pin31, IC3.pin32, IC4.pin9, IC4.pin10, IC4.pin11, IC4.pin12, IC4.pin14, IC5.pin1, IC5.pin2, IC5.pin3, IC5.pin30, IC5.pin31, IC5.pin32
  N17: J3.pin2, J4.pin14, IC5.pin17
  N18: J3.pin3, J4.pin13, IC5.pin15
  N19: J3.pin4, J4.pin12, IC5.pin14
  N20: J3.pin5, J4.pin11, IC5.pin13
  N21: J3.pin6, J4.pin10, IC5.pin12
  N22: J3.pin7, J4.pin9, IC5.pin11
  N23: J3.pin8, J4.pin8, IC5.pin10
  N24: J3.pin9, J4.pin7, IC5.pin9
  N25: J3.pin10, J4.pin6, IC5.pin8
  N26: J3.pin11, J4.pin5, IC5.pin7
  N27: J3.pin12, J4.pin4, IC5.pin6
  N28: J3.pin13, J4.pin3, J8.pin8, J5.pin8, IC5.pin23
  N29: J3.pin14, J4.pin2, IC5.pin24
  N30: J6.pin1, J7.pin15, J8.pin1, J5.pin15
  N31: J6.pin2, J7.pin14, IC2.pin24, IC3.pin24, IC4.pin1
  N32: J6.pin3, J7.pin13, IC1_2.pin11, IC2.pin13, IC3.pin13
  N33: J6.pin4, J7.pin12, IC1_2.pin12, IC2.pin14, IC3.pin14
  N34: J6.pin5, J7.pin11, IC1_2.pin13, IC2.pin15, IC3.pin15
  N35: J6.pin6, J7.pin10, IC1_2.pin15, IC2.pin17, IC3.pin17
  N36: J6.pin7, J7.pin9, IC1_2.pin16, IC2.pin18, IC3.pin18
  N37: J6.pin8, J7.pin8, IC1_2.pin17, IC2.pin19, IC3.pin19
  N38: J6.pin9, J7.pin7, IC1_2.pin18, IC2.pin20, IC3.pin20
  N39: J6.pin10, J7.pin6, IC1_2.pin19, IC2.pin21, IC3.pin21
  N40: J6.pin11, J7.pin5, Pad16.pad, Pad17.pad, IC4.pin4, IC4.pin13
  N41: J6.pin12, J7.pin4, IC2.pin28, IC3.pin28, IC4.pin2
  N42: J6.pin13, J7.pin3, IC1_2.pin2, IC2.pin4, IC3.pin4
  N43: J6.pin14, J7.pin2, IC4.pin5
  N44: J8.pin2, J5.pin14
  N45: J8.pin3, J8.pin4, J5.pin12, J5.pin13
  N46: J8.pin5, J5.pin11, IC5.pin5
  N47: J8.pin6, J5.pin10, IC5.pin27
  N48: J8.pin7, J5.pin9, IC5.pin26
  N49: J8.pin9, J5.pin7, IC5.pin25
  N50: J8.pin10, J5.pin6, IC5.pin4
  N51: J8.pin11, J5.pin5, IC5.pin22
  N52: J8.pin12, J5.pin4, IC5.pin21
  N53: J8.pin13, J5.pin3, IC5.pin20
  N54: J8.pin14, J5.pin2, IC5.pin19
  N55: J8.pin15, J5.pin1, IC5.pin18
  N56: C1.1, IC1.pin10, IC4.pin6
  N57: C5.1, D2.cathode, D1.cathode, R1.Pin_1, IC1_2.pin1, IC1_2.pin26, IC1_2.pin28
  N58: D1.anode, BAT.+
  N59: R1.Pin_0, IC1.pin1, IC1_2.pin20
  N60: IC1.pin2, R2.Pin_1, Pad21.pad, Pad22.pad
  N61: IC1.pin3, R3.Pin_1, Pad20.pad
  N62: IC1.pin4, R4.Pin_1, Pad5.pad
  N63: IC1.pin5, R5.Pin_1, Pad4.pad
  N64: Pad3.pad, IC5.pin29
  N65: Pad6.pad, IC5.pin28
  N66: Pad9.pad, IC1_2.pin23
  N67: Pad12.pad, IC2.pin22
  N68: Pad13.pad, IC4.pin8
  N69: Pad15.pad, IC3.pin22
  N70: Pad18.pad, IC2.pin29, IC3.pin29
  N71: Pad19.pad, Pad25.pad
  N72: Pad23.pad, IC2.pin2, IC3.pin2
  N73: Pad24.pad, IC2.pin3, IC3.pin3

notes:
  1
  30
  31
  60
  A14
  A13
  64K
  256K
  128K
  CHARACTER ROM SIZE
  -------  -------
  ----  ----
  RAM SIZE
  24PIN
  28PIN
  A15
  A16
  #CE
  WP
  PRG
  CHR
  NUM PRG ROMS
  PRG ROM SIZE
  32PIN
  1x
  2x
  ------------
  IC1 WORKING RAM
  IC2 PROGRAM ROM A
  IC3 PROGRAM ROM B
  IC4 74LS20
  IC5 CHARACTER ROM C
  VCC
  A12
  A7
  A6
  A5
  A4
  A3
  A2
  A1
  A0
  D0
  D1
  D2
  GND
  #WE
  A8
  A9
  A11
  #OE
  A10
  D7
  D6
  D5
  D4
  D3
  1A
  1B
  1C
  1D
  1Y
  2D
  2C
  2B
  2A
  2Y
  -
  +
  5.1K
  10K
  68P
