# Fritzing sketch famikeys (saved by Fritzing 0.9.3b)
circuit board: 6.88566cm x 5.36311cm
breadboards: 1

parts:
  PCB1 = Arduino Shield PCB  # not connected
  J7 = female pin header, 6 pins [form="♀ (female)"]
  J8 = female pin header, 8 pins [form="♀ (female)"]
  S9 = Toggle Switch [package=THT]
  S10 = Pushbutton [package="[THT]"]
  J9 = female pin header, 8 pins [form="♀ (female)"]
  J10 = female pin header, 10 pins [form="♀ (female)"]
  S11 = Toggle Switch [package=THT]
  S12 = Toggle Switch [package=THT]
  S13 = Toggle Switch [package=THT]
  S14 = Toggle Switch [package=THT]
  X1 = DB15 Connector [package=db15]
  J11 = female pin header, 15 pins [form="♀ (female)"]
  J12 = female pin header, 15 pins [form="♀ (female)"]
  X2 = DB15 Connector [package=db15]

nets:
  N1: J7.pin1, X1.2, J11.pin3, J12.pin3, X2.7
  N2: J7.pin2, X1.3, J11.pin5, J12.pin5, X2.6
  N3: J7.pin3, X1.4, J11.pin7, J12.pin7, X2.5
  N4: J7.pin4, X1.5, J11.pin9, J12.pin9, X2.4
  N5: J7.pin5, X1.12, J11.pin8, J12.pin8, X2.12
  N6: J7.pin6, X1.13, J11.pin10, J12.pin10, X2.11
  N7: J8.pin3, S10.Pin_3, S10.Pin_4
  N8: J8.pin5, S9.L1
  N9: J8.pin6, J8.pin7, S10.Pin_1, S10.Pin_2, X1.8, J11.pin15, J12.pin15, X2.1
  N10: J8.pin8, S9.L2
  N11: S9.COM, X1.9, J11.pin2, J12.pin2, X2.15
  N12: J9.pin2, X1.14, J11.pin12, J12.pin12, X2.10
  N13: J9.pin3, S14.L1, S14.COM
  N14: J9.pin4, S13.L1, S13.COM
  N15: J9.pin5, S12.L1, S12.COM
  N16: J9.pin6, S11.L1, S11.COM
  N17: J10.pin4, S11.L2, S12.L2, S13.L2, S14.L2
  N18: X1.1, J11.pin1, J12.pin1, X2.8
  N19: X1.6, J11.pin11, J12.pin11, X2.3
  N20: X1.7, J11.pin13, J12.pin13, X2.2
  N21: X1.10, J11.pin4, J12.pin4, X2.14
  N22: X1.11, J11.pin6, J12.pin6, X2.13
  N23: X1.15, J11.pin14, J12.pin14, X2.9

notes:
  KBD PWR
  RESET
  Vin
  5V
  SER
  USB
  FK>
  >FH
  Emulator
  Translator/
  Tester/
  Keyboard
  D
  C
  B
  A
  01 GND
  02 SND
  03 IRQ
  04 DA4
  05 DA3
  06 DA2
  07 DA1
  08 DA0
  09 OE2
  10 ENA
  11 INC
  12 RST
  13 CIN
  14 OE1
  15 VCC
  VCC 15
  DA1 07
  IRQ 03
  DA2 06
  DA4 04
  INC 11
  DA3 05
  OE2 09
  SND 02
  DA0 08
  CIN 13
  OE1 14
  GND 01
  ENA 10
  RST 12
  DA15M
  to Keyboard
  DA15F
  to Famicom

custom parts:
  Arduino Shield PCB: Plain PCB Shaped to fit an Arduino "Shield"
  DB15 Connector: DB15 Connector Standard DB15 (D-Sub 15) pc midi or gameport connector. Can be used for old PC compatible joystic.
